# Fritzing sketch WiTcontroller - 4x4 keypad, Optional buttons v0.1 (saved by Fritzing 0.9.3b)

parts:
  MCU1 = Wemos Lolin32lite
  RE4 = KY-040 Rotary encoder [package=THT]
  o1 = Module display OLED I2C 128x64 SSD1306 [package=THT]
  S1 = Momentary Switch [package=ksa_sealed_tac_switch]
  S2 = Momentary Switch [package=ksa_sealed_tac_switch]
  S3 = Momentary Switch [package=ksa_sealed_tac_switch]
  S4 = Momentary Switch [package=ksa_sealed_tac_switch]
  S5 = Momentary Switch [package=ksa_sealed_tac_switch]
  S6 = Momentary Switch [package=ksa_sealed_tac_switch]
  Matrix_keypad1 = KEYPAD 4x4

nets:
  N1: MCU1.pin_6, S6.2
  N2: MCU1.pin_7, Matrix_keypad1.col4
  N3: MCU1.pin_8, S3.2
  N4: MCU1.pin_9, S4.2
  N5: MCU1.pin_10, S5.2
  N6: MCU1.pin_11, RE4.CLK
  GND: MCU1.pin_12, MCU1.pin_13, RE4.GND, RE4.DT, o1.GND, S1.3, S2.3, S3.3, S4.3, S5.3, S6.3
  N7: MCU1.pin_16, RE4.SW
  N8: MCU1.pin_17, S2.2
  N9: MCU1.pin_18, Matrix_keypad1.col3
  N10: MCU1.pin_19, Matrix_keypad1.col2
  N11: MCU1.pin_20, Matrix_keypad1.col1
  N12: MCU1.pin_21, MCU1.pin_22, Matrix_keypad1.row3, Matrix_keypad1.row4
  N13: MCU1.pin_23, S1.2
  N14: MCU1.pin_24, Matrix_keypad1.row2
  N15: MCU1.pin_25, o1.SDA
  N16: MCU1.pin_26, Matrix_keypad1.row1
  N17: MCU1.pin_27, o1.SCL
  VCC: MCU1.pin_28, RE4.Vcc, o1.VCC

notes:
  6 Optional Additional Buttons

custom parts:
  Wemos Lolin32lite: Wemos Lolinlite32 wifi and blue tooth board based on the ESP-32 cpu, digital I/Os 19, analog inputs 6, clock 240mhz, Flash 4Mbytes, lipo battery charger (500ma connection broken out on breadboard but not pcb), usb.
  KY-040 Rotary encoder: KY-040 Rotary Encoder with switch on breakout borad from AZ Delivery
  Module display OLED I2C 128x64 SSD1306: Ecran OLED I2C SSD163 de 128x64 avec connexion I2C
  KEYPAD 4x4: Matrix keypad 16 buttons, 4 rows x 4 columns
