# Fritzing sketch WiTcontroller v0.1 (saved by Fritzing 0.9.3b)

parts:
  MCU1 = Wemos Lolin32lite
  RE4 = KY-040 Rotary encoder [package=THT]
  kEYPAD_MATRICIAL_1 = KEYPAD 4x3
  o1 = Module display OLED I2C 128x64 SSD1306 [package=THT]

nets:
  N1: MCU1.pin_11, RE4.CLK
  GND: MCU1.pin_12, MCU1.pin_13, RE4.GND, RE4.DT, o1.GND
  N2: MCU1.pin_16, RE4.SW
  N3: MCU1.pin_18, kEYPAD_MATRICIAL_1.col3
  N4: MCU1.pin_19, kEYPAD_MATRICIAL_1.col1
  N5: MCU1.pin_20, kEYPAD_MATRICIAL_1.col2
  N6: MCU1.pin_21, MCU1.pin_22, kEYPAD_MATRICIAL_1.arrow2, kEYPAD_MATRICIAL_1.arrow3
  N7: MCU1.pin_24, kEYPAD_MATRICIAL_1.arrow4
  N8: MCU1.pin_25, o1.SDA
  N9: MCU1.pin_26, kEYPAD_MATRICIAL_1.arrow1
  N10: MCU1.pin_27, o1.SCL
  VCC: MCU1.pin_28, RE4.Vcc, o1.VCC

custom parts:
  Wemos Lolin32lite: Wemos Lolinlite32 wifi and blue tooth board based on the ESP-32 cpu, digital I/Os 19, analog inputs 6, clock 240mhz, Flash 4Mbytes, lipo battery charger (500ma connection broken out on breadboard but not pcb), usb.
  KY-040 Rotary encoder: KY-040 Rotary Encoder with switch on breakout borad from AZ Delivery
  KEYPAD 4x3: KEYPAD matricial de 12 botones, 4 filas x 3 columnas
  Module display OLED I2C 128x64 SSD1306: Ecran OLED I2C SSD163 de 128x64 avec connexion I2C
