# Fritzing sketch WiTcontroller - 3x4 keypad, Optional buttons - pullups (saved by Fritzing 0.9.3b)

parts:
  MCU1 = Wemos Lolin32lite
  RE4 = KY-040 Rotary encoder [package=THT]
  o1 = Module display OLED I2C 128x64 SSD1306 [package=THT]
  S1 = Momentary Switch [package=ksa_sealed_tac_switch]
  S2 = Momentary Switch [package=ksa_sealed_tac_switch]
  S3 = Momentary Switch [package=ksa_sealed_tac_switch]
  S4 = Momentary Switch [package=ksa_sealed_tac_switch]
  S5 = Momentary Switch [package=ksa_sealed_tac_switch]
  S6 = Momentary Switch [package=ksa_sealed_tac_switch]
  S9 = Momentary Switch [package=ksa_sealed_tac_switch]
  S10 = Momentary Switch [package=ksa_sealed_tac_switch]
  S11 = Momentary Switch [package=ksa_sealed_tac_switch]
  S12 = Momentary Switch [package=ksa_sealed_tac_switch]
  R3 = Resistor [tolerance=±1% resistance=10 package=THT]
  R4 = Resistor [tolerance=±1% resistance=10 package=THT]
  R5 = Resistor [tolerance=±1% resistance=10 package=THT]
  R6 = Resistor [tolerance=±1% resistance=10 package=THT]
  S13 = Momentary Switch [package=ksa_sealed_tac_switch]  # not connected
  kEYPAD_MATRICIAL_2 = KEYPAD 4x3  # not connected

nets:
  N1: MCU1.pin_1, S10.2, R5.Pin_0
  N2: MCU1.pin_2, S9.2, R6.Pin_0
  N3: MCU1.pin_4, S12.2, R3.Pin_0
  N4: MCU1.pin_5, S11.2, R4.Pin_0
  N5: MCU1.pin_6, S6.2
  N6: MCU1.pin_8, S3.2
  N7: MCU1.pin_9, S4.2
  N8: MCU1.pin_10, S5.2
  N9: MCU1.pin_11, RE4.CLK
  GND: MCU1.pin_12, MCU1.pin_13, RE4.GND, RE4.DT, o1.GND, S1.3, S2.3, S3.3, S4.3, S5.3, S6.3, S12.3
  N10: MCU1.pin_16, RE4.SW
  N11: MCU1.pin_17, S2.2
  N12: MCU1.pin_23, S1.2
  N13: MCU1.pin_25, o1.SDA
  N14: MCU1.pin_27, o1.SCL
  VCC: MCU1.pin_28, RE4.Vcc, o1.VCC, R6.Pin_1

notes:
  7 Optional Additional Buttons
  - don't require the pullup resistor
  4 Optional Additional Buttons
  - Require 10k pullup resistor

custom parts:
  Wemos Lolin32lite: Wemos Lolinlite32 wifi and blue tooth board based on the ESP-32 cpu, digital I/Os 19, analog inputs 6, clock 240mhz, Flash 4Mbytes, lipo battery charger (500ma connection broken out on breadboard but not pcb), usb.
  KY-040 Rotary encoder: KY-040 Rotary Encoder with switch on breakout borad from AZ Delivery
  Module display OLED I2C 128x64 SSD1306: Ecran OLED I2C SSD163 de 128x64 avec connexion I2C
  KEYPAD 4x3: KEYPAD matricial de 12 botones, 4 filas x 3 columnas
